# Fritzing sketch PSoC_PyunPyun_3rdLPF (saved by Fritzing 0.9.2b)
breadboards: 2
perfboards: 1

parts:
  IC1 = Dual Op-Amp [package=dip08]
  C1 = Ceramic Capacitor [capacitance=0.1nF package="100 mil [THT, multilayer]"]
  R1 = Resistor [tolerance=±5% resistance=3.3k package=THT]
  C2 = Ceramic Capacitor [capacitance=3.9nF package="100 mil [THT, multilayer]"]
  R2 = Resistor [tolerance=±5% resistance=100k package=THT]
  C3 = Ceramic Capacitor [capacitance=100nF package="100 mil [THT, multilayer]"]
  R3 = Resistor [tolerance=±5% resistance=10k package=THT]
  R4 = Resistor [tolerance=±5% resistance=2.2k package=THT]
  C4 = Ceramic Capacitor [capacitance=100nF package="100 mil [THT, multilayer]"]
  C5 = Ceramic Capacitor [capacitance=100nF package="100 mil [THT, multilayer]"]
  C6 = Electrolytic Capacitor [capacitance=47µF package="100 mil [THT, electrolytic]"]
  C7 = Electrolytic Capacitor [capacitance=47µF package="100 mil [THT, electrolytic]"]
  R5 = Resistor [tolerance=±5% resistance=10k package=THT]
  R6 = Resistor [tolerance=±5% resistance=10k package=THT]
  J8 = female pin header, 10 pins [form="♀ (female)"]
  J9 = female pin header, 8 pins [form="♀ (female)"]  # not connected
  J10 = female pin header, 8 pins [form="♀ (female)"]
  J11 = female pin header, 9 pins [form="♀ (female)"]
  J12 = female pin header, 9 pins [form="♀ (female)"]  # not connected
  J13 = female pin header, 6 pins [form="♀ (female)"]  # not connected
  J14 = female pin header, 6 pins [form="♀ (female)"]  # not connected
  U1 = mystery part, 9 pins [chip_label=SPLC792-I2C]
  R7 = Resistor [tolerance=±5% resistance=1k package=THT]
  R8 = Resistor [tolerance=±5% resistance=10k package=THT]
  C8 = Electrolytic Capacitor [capacitance=0.22mF package="100 mil [THT, electrolytic]"]
  J15 = female pin header, 1 pin [form="♀ (female)"]
  U2 = mystery part, 7 pins [chip_label="PyunPyun Controller"]

nets:
  N1: IC1.A_OUT, IC1.A_-IN, C2.1, C8.+
  N2: IC1.A_+IN, C1.0, R1.Pin_1
  N3: IC1.A_V-, C4.0, C7.-, R6.Pin_1, J10.pin6, U1.pin2, U1.pin6, U1.pin9, U2.pin7
  N4: IC1.B_+IN, C6.-, C7.+, R5.Pin_1, R6.Pin_0
  N5: IC1.B_-IN, IC1.B_OUT, C5.1
  N6: IC1.A_V+, C5.0, C6.+, R5.Pin_0
  N7: C1.1, C3.1, R4.Pin_1, C4.1, J11.pin7, R8.Pin_1
  N8: R1.Pin_0, C2.0, R2.Pin_1
  N9: R2.Pin_0, C3.0, R3.Pin_1
  N10: R3.Pin_0, R4.Pin_0, J8.pin9
  N11: J8.pin1, U1.pin4
  N12: J8.pin2, U1.pin5
  N13: J8.pin5, U1.pin3
  N14: J10.pin4, U2.pin6
  N15: J10.pin5, R7.Pin_1
  N16: J11.pin1, U2.pin5
  N17: J11.pin2, U2.pin4
  N18: J11.pin3, U2.pin3
  N19: J11.pin4, U2.pin2
  N20: J11.pin5, U2.pin1
  N21: U1.pin1, R7.Pin_0
  N22: R8.Pin_0, C8.-, J15.pin1

notes:
  AGND
  +5V
  0V
  AGND
  0V
  +3.3V
  PSoC 4
  Pioneer Kit
